# Fritzing sketch nightlight (saved by Fritzing 0.9.3b)
circuit board: 8.46667cm x 5.64444cm
breadboards: 1

parts:
  Part1 = Arduino Uno (Rev3)
  Resistor = Resistor [tolerance=±5% resistance=470 package=THT]
  LED = LED - 5mm [color="Red (633nm)" package="5 mm [THT]"]
  Resistor_2 = Resistor [tolerance=±5% resistance=10k package=THT]
  Photoresistor = Photocell (LDR) [package=THT]

nets:
  N1: Part1.A0, Resistor_2.Pin_0, Photoresistor.pin_1
  N2: Part1.D12/MISO, LED.anode
  N3: Part1.5V, Photoresistor.pin_0
  N4: Part1.GND, Resistor.Pin_0, Resistor_2.Pin_1
  N5: Resistor.Pin_1, LED.cathode

// code stored in the sketch: nightlight.ino
/** 
 * Arduino Tutorial: Learn how to use analog input and digital output
 * More info: https://github.com/RochesterMakerSpace/ArduinoClass
 */

// Initialize the Arduino
setup() {
  pinMode(12,OUTPUT);
}

// Loop forever checking the status of the photoresistor and controlling the LED
loop() {
	// Read the photoresistor value (0-1024)
    int sensorValue = analogRead(A0);

    // Adjust the sensitivity as desired.  Initial value is 500.
    if (sensorValue < 500) {
		// It's dark.  Turn on the LED.
        digitalWrite(12,HIGH);
    } else {
		// It's not too dark.  Turn off the LED.
        digitalWrite(12,LOW);
    }
	
	// No real need to delay here, but a delay can help avoid flickering
    // when the light level is close to the threshold value.
    delay(10);
}
